// Logisim project 18_1b.circ as structural Verilog: 1 circuit, main circuit main
module main (
  input  A,
  input  B,
  input  C,
  input  D,
  output out_5,
  output out_6
);

  wire nand_1_out, nand_2_out, nand_3_out, not_1_out, not_2_out, not_3_out, not_4_out, or_1_out, or_2_out,
       or_3_out;

  not not_1 (not_1_out, A);
  not not_2 (not_2_out, B);
  not not_3 (not_3_out, C);
  not not_4 (not_4_out, D);
  nand nand_1 (nand_1_out, not_1_out, D);
  nand nand_2 (nand_2_out, B, D);
  nand nand_3 (nand_3_out, not_1_out, C);
  or or_1 (or_1_out, C, D);
  or or_2 (or_2_out, not_1_out, B);
  or or_3 (or_3_out, not_1_out, D);
  and F1 (out_5, nand_1_out, nand_2_out, nand_3_out);
  nand F2 (out_6, or_1_out, or_2_out, or_3_out);
endmodule
