// Logisim project 1905113.circ as structural Verilog: 2 circuits, main circuit problem1
module problem1 (
  input  J,
  input  K,
  output Q,
  output Q_prime
);

  wire clock_1_out, n7400_1_p2, n7400_1_p3, n7400_1_p11, n7400_2_p3, n7400_2_p6, n7410_1_p9, n7410_1_p13;

  Clock clock_1 (.out(clock_1_out));
  // _7410 7410_1: pin names not known; wires that end beside it: clock_1_out, J, K, clock_1_out, J, clock_1_out, Q, K, n7410_1_p9, 1'b0, 1'b1, Q_prime, n7410_1_p13
  // _7400 7400_1: pin names not known; wires that end beside it: n7410_1_p13, n7400_1_p2, n7400_1_p3, n7410_1_p9, n7400_1_p3, n7400_1_p2, 1'b0, 1'b1, clock_1_out, clock_1_out, n7400_1_p11
  // _7400 7400_2: pin names not known; wires that end beside it: n7400_1_p11, n7400_1_p3, n7400_2_p3, n7400_1_p11, n7400_1_p2, n7400_2_p6, 1'b0, 1'b1, n7400_2_p3, Q_prime, Q, Q, n7400_2_p6, Q_prime
endmodule

module Problem2 (
  input  nCLR,
  input  S1,
  input  S0,
  input  I3,
  input  I2,
  input  I1,
  input  I0,
  input  Serial_input_for_shift_left,
  input  Serial_input_for_shift_right,
  output A3,
  output A2,
  output A1,
  output A0
);

  wire CLK_out, n7474_1_p8, n7474_1_p9, n7474_2_p8, n7474_2_p9, not_1_out;

  Clock CLK (.out(CLK_out));
  not not_1 (not_1_out, nCLR);
  // _7474 7474_1: pin names not known; wires that end beside it: 1'b0, A2, A3, 1'b0, 1'b0, CLK_out, CLK_out, n7474_1_p8, n7474_1_p9, not_1_out, not_1_out, 1'b1
  // _74153 74153_1: pin names not known; wires that end beside it: 1'b0, n7474_1_p8, n7474_1_p9, A2, A3, A3, Serial_input_for_shift_right, A1, A2, I2, I3, S0, S1, 1'b0, 1'b0, 1'b1
  // _7474 7474_2: pin names not known; wires that end beside it: 1'b0, A0, A1, 1'b0, 1'b0, CLK_out, CLK_out, n7474_2_p8, n7474_2_p9, not_1_out, not_1_out, 1'b1, not_1_out, CLK_out, 1'b0
  // _74153 74153_2: pin names not known; wires that end beside it: 1'b0, n7474_2_p8, n7474_2_p9, A0, A1, A1, A2, Serial_input_for_shift_left, A0, I0, I1, S0, S1, 1'b0, 1'b0, 1'b1
endmodule
