// Logisim project 1905113.circ as structural Verilog: 1 circuit, main circuit 1905113
module _1905113 (
  input  W,
  input  X,
  input  Y,
  input  Z,
  output out_5
);

  wire and_1_out, and_2_out, and_3_out, n74138_1_p8, n74138_1_p9, n74138_2_p14, n74138_2_p15, n74138_2_p16,
       n74138_2_p17, not_1_out;

  not not_1 (not_1_out, W);
  // _74138 74138_1: pin names not known; wires that end beside it: Z, Y, X, not_1_out, 1'b0, 1'b1, 1'b1, n74138_1_p8, n74138_1_p9
  // _74138 74138_2: pin names not known; wires that end beside it: W, X, Y, Z, 1'b0, Z, Y, X, W, 1'b0, 1'b1, 1'b0, 1'b1, n74138_2_p14, n74138_2_p15, n74138_2_p16, n74138_2_p17
  and and_1 (and_1_out, n74138_1_p8, n74138_1_p9);
  and and_2 (and_2_out, n74138_2_p14, n74138_2_p15, n74138_2_p16, n74138_2_p17);
  and and_3 (and_3_out, and_1_out, and_2_out);
  not not_2 (out_5, and_3_out);
endmodule
