// Logisim project 1905113.circ as structural Verilog: 1 circuit, main circuit main
module main (
  input  A,
  input  B,
  input  C,
  input  D,
  output out_5
);

  wire n7404_1_p2, n7432_1_p8;

  // _7404 7404_1: pin names not known; wires that end beside it: C, n7404_1_p2, 1'b0, 1'b1
  // _7432 7432_1: pin names not known; wires that end beside it: A, B, C, D, 1'b1, C, D, n7432_1_p8, 1'b0, 1'b1, 1'b0
  // _74153 74153_1: pin names not known; wires that end beside it: 1'b0, A, n7404_1_p2, 1'b1, D, n7432_1_p8, out_5, 1'b1, 1'b0, B
endmodule
