// Logisim project Test.circ as structural Verilog: 1 circuit, main circuit main
module main (
  output out_1,
  output out_2,
  output out_3
);

  wire CLK_out, n7408_1_p2, n7432_1_p7, n7432_1_p8, n7474_1_p2, n7474_1_p6, n7474_1_p10;

  Clock CLK (.out(CLK_out));
  // _7474 7474_1: pin names not known; wires that end beside it: 1'b0, n7474_1_p2, CLK_out, 1'b0, out_1, n7474_1_p6, 1'b0, 1'b1, 1'b0, n7474_1_p10, CLK_out, 1'b0, out_2, n7474_1_p10
  // _7432 7432_1: pin names not known; wires that end beside it: out_2, out_3, n7474_1_p2, 1'b0, 1'b1, n7474_1_p6, n7432_1_p7, n7432_1_p8
  // _7408 7408_1: pin names not known; wires that end beside it: n7474_1_p10, n7408_1_p2, n7432_1_p7, 1'b0, 1'b1
  // _7474 7474_2: pin names not known; wires that end beside it: 1'b0, n7432_1_p8, CLK_out, 1'b0, out_3, n7408_1_p2, 1'b0, 1'b1
endmodule
