// Logisim project 1905113.circ as structural Verilog: 1 circuit, main circuit main
module main (
  output Y2,
  output Y1,
  output Y0
);

  wire clock_1_out, n7432_1_p1, n7476_1_p4, n7476_1_p11, n7476_1_p13, n7476_1_p15;

  Clock clock_1 (.out(clock_1_out));
  // _7476 7476_1: pin names not known; wires that end beside it: clock_1_out, 1'b0, 1'b0, n7476_1_p4, 1'b1, clock_1_out, 1'b0, 1'b0, 1'b1, Y2, n7476_1_p11, 1'b0, n7476_1_p13, Y1, n7476_1_p15, 1'b1
  // _7432 7432_1: pin names not known; wires that end beside it: n7432_1_p1, n7476_1_p15, n7476_1_p4, n7476_1_p11, n7432_1_p1, n7476_1_p13, 1'b0, 1'b1
  // _7476 7476_2: pin names not known; wires that end beside it: clock_1_out, 1'b0, 1'b0, Y1, 1'b1, Y1, Y0, n7432_1_p1, 1'b0

  // Notes on the sheet:
  //   Sequence:
  //   6-1-7-2-5-3-0
endmodule
