// Logisim project 1905113.circ as structural Verilog: 1 circuit, main circuit main
module main (
  input  A,
  input  B,
  input  C,
  input  D
);

  wire n7404_1_p6, n7404_1_p8;

  // _7404 7404_1: pin names not known; wires that end beside it: A, B, C, D, 1'b1, n7404_1_p6, A, n7404_1_p8, D, n7404_1_p6, 1'b0, 1'b1
  // _74153 74153_1: pin names not known; wires that end beside it: A, B, 1'b0, 1'b1, n7404_1_p8, C
  // _7432 7432_1: pin names not known; wires that end beside it: 1'b0, 1'b1
endmodule
