// Logisim project 1905113.circ as structural Verilog: 3 circuits, main circuit main
module main (
  input  [3:0] X,
  output F_X
);

  wire n7404_1_p2, n7404_1_p4, n7404_1_p6, n7408_1_p3, n7408_1_p6, n7408_1_p9, n7408_1_p11, n7408_1_p12,
       n7408_1_p14;

  // _7404 7404_1: pin names not known; wires that end beside it: X[1], n7404_1_p2, X[2], n7404_1_p4, X[3], n7404_1_p6, 1'b0, 1'b1
  // _7408 7408_1: pin names not known; wires that end beside it: n7404_1_p2, n7404_1_p4, n7408_1_p3, X[0], X[2], n7408_1_p6, 1'b0, 1'b1, n7408_1_p9, n7404_1_p6, n7408_1_p11, n7408_1_p12, n7408_1_p6, n7408_1_p14
  // _7432 7432_1: pin names not known; wires that end beside it: n7408_1_p3, n7408_1_p6, n7408_1_p9, X[3], n7404_1_p2, n7408_1_p12, 1'b0, 1'b1, n7408_1_p14, n7408_1_p11, F_X
endmodule

module s2 (
  input  [3:0] in_1,
  output F_X,
  output F_prime_X
);

  main main_1 (.X(in_1), .F_X(F_X));
  // _7404 7404_1: pin names not known; wires that end beside it: F_X, F_prime_X, 1'b0, 1'b1
endmodule

module s3 (
  input  [3:0] A,
  input  [3:0] B,
  output F_A__prime_F_B__F_A_F_B__prime
);

  wire n7408_1_p3, n7408_1_p6, s2_1_f_prime_x, s2_1_f_x, s2_2_f_prime_x, s2_2_f_x;

  s2 s2_1 (.in_1(A), .F_X(s2_1_f_x), .F_prime_X(s2_1_f_prime_x));
  s2 s2_2 (.in_1(B), .F_X(s2_2_f_x), .F_prime_X(s2_2_f_prime_x));
  // _7408 7408_1: pin names not known; wires that end beside it: s2_1_f_prime_x, s2_2_f_x, n7408_1_p3, s2_1_f_x, s2_2_f_prime_x, n7408_1_p6, 1'b0, 1'b1
  // _7432 7432_1: pin names not known; wires that end beside it: n7408_1_p3, n7408_1_p6, F_A__prime_F_B__F_A_F_B__prime, 1'b0, 1'b1
endmodule
