// Logisim project test.circ as structural Verilog: 1 circuit, main circuit main
module main (
  input  I3,
  input  I2,
  input  I1,
  input  I0,
  output s1,
  output s0
);

  wire n7432_1_p9;

  // _7432 7432_1: pin names not known; wires that end beside it: I2, I1, I0, I2, I3, s1, I2, I0, n7432_1_p9, 1'b0, 1'b1
  // _7404 7404_1: pin names not known; wires that end beside it: n7432_1_p9, s0, 1'b0, 1'b1
endmodule
