// Logisim project practiseForOnline1.circ as structural Verilog: 3 circuits, main circuit main
module main (
  input  [2:0] A,
  input  [2:0] B,
  output [2:0] out_3,
  output [2:0] out_4
);

  wire [2:0] A_out, and_1_out, and_2_out, not_1_out;

  assign A_out = ~A;  // NOT_Gate A, 3 bits wide
  assign not_1_out = ~B;  // NOT_Gate not_1, 3 bits wide
  assign and_1_out = A & not_1_out;  // AND_Gate and_1, 3 bits wide
  assign and_2_out = A_out & B;  // AND_Gate and_2, 3 bits wide
  assign out_4 = A | B;  // OR_Gate Y, 3 bits wide
  assign out_3 = and_1_out | and_2_out;  // OR_Gate X, 3 bits wide
endmodule

module another (
  input  [2:0] in_1,
  input  [2:0] in_2,
  input  in_3,
  input  in_4,
  output [2:0] out_5,
  output [2:0] out_6,
  output out_7,
  output out_8
);

  main main_1 (.A(in_1), .B(in_2), .out_3(out_5), .out_4(out_6));
  withIC withic_1 (.A(in_4), .B(in_3), .out_3(out_7), .out_4(out_8));
endmodule

module withIC (
  input  A,
  input  B,
  output out_3,
  output out_4
);

  wire n7404_1_p2, n7404_1_p4, n7408_1_p3, n7408_1_p6;

  // _7404 7404_1: pin names not known; wires that end beside it: 1'b0, n7404_1_p2, B, n7404_1_p4, A, 1'b1
  // _7408 7408_1: pin names not known; wires that end beside it: A, n7404_1_p2, n7408_1_p3, n7404_1_p4, B, n7408_1_p6, 1'b0, 1'b1
  // _7432 7432_1: pin names not known; wires that end beside it: n7408_1_p6, n7408_1_p3, out_3, A, B, out_4, 1'b0, 1'b1
endmodule
